# Fritzing sketch 7 control rele (saved by Fritzing 0.9.3b)

parts:
  Componente1 = Arduino Sensor Shield v5.0
  U1 = 4-Channel 5v Relay Shield [package=relay-4ch5v10a]

nets:
  +5V: Componente1.+5V, Componente1.D9, Componente1.D11, Componente1.D10, U1.VCC, U1.IN2, U1.IN4, U1.IN3
  N1: Componente1.D8, U1.IN1
  GND: Componente1.GND, U1.GND

custom parts:
  4-Channel 5v Relay Shield: 4 Channel 5v Relay Shield w. 2x SPD-06VDC-SD-C
