# Fritzing sketch AQMNode (saved by Fritzing 0.9.2b)
breadboards: 1

parts:
  Edison+Breakout = Intel Edison Arduinobreakout
  MQ2 = Header 4 [package=molex-1x4_lock]
  MQ5 = Header 4 [package=molex-1x4_lock]
  TP401 = Header 4 [package=molex-1x4_lock]
  MQ9 = Header 4 [package=molex-1x4_lock]
  GPS = Header 4 [package=molex-1x4_lock]

nets:
  N1: Edison+Breakout.A0, MQ2.1
  N2: Edison+Breakout.A1, MQ5.1
  N3: Edison+Breakout.A2, TP401.1
  N4: Edison+Breakout.A3, MQ9.1
  N5: Edison+Breakout.D1/TX, GPS.1
  N6: Edison+Breakout.5V, MQ2.3, MQ5.3, MQ9.3, GPS.3
  N7: Edison+Breakout.GND, MQ2.4, MQ5.4, TP401.4, MQ9.4, GPS.4

notes:
  TX
  RX
  These Sensors: SIG  NC  VCC  GND
  MQ2
  MQ5
  MQ9
  TP401
  GPS
